// Logisim project AddSubbOfSignNum.circ as structural Verilog: 1 circuit, main circuit main
module main (
  input  As,
  input  Bs,
  input  [4:0] _20,
  input  [4:0] _9,
  input  As_2,
  input  Bs_2,
  input  in_7,
  input  in_8,
  input  in_9,
  input  [4:0] in_10,
  input  [4:0] in_11,
  output out_12,
  output [4:0] out_13,
  output out_14,
  output out_15,
  output [4:0] out_16,
  output A_B,
  output out_18,
  output out_19,
  output [4:0] out_20,
  output A_B_2,
  output out_22,
  output out_23,
  output [4:0] out_24,
  output A_B_3,
  output [4:0] out_26
);

  wire adder_1_cout, adder_3_cout, comparator_1_gt, comparator_1_lt, not_2_out, not_6_out, or_1_out,
       or_2_out, undriven, xor_1_out, xor_2_out;
  wire [4:0] adder_1_out, adder_3_out, controlled_buffer_2_out, not_1_out, not_4_out;

  xor xor_1 (xor_1_out, As, Bs);
  or or_1 (or_1_out, xor_1_out, in_8);
  assign not_1_out = ~_9;  // NOT_Gate not_1, 5 bits wide
  not not_2 (not_2_out, or_1_out);
  not not_3 (out_18, As);
  assign out_16 = not_2_out ? adder_1_out : 5'bz;  // Controlled_Buffer controlled_buffer_1
  Adder #(.width(5)) adder_1 (.a(_20), .b(not_1_out), .out(adder_1_out), .cin(1'b1), .cout(adder_1_cout));
  assign not_4_out = ~out_16;  // NOT_Gate not_4, 5 bits wide
  not not_5 (A_B, adder_1_cout);
  assign controlled_buffer_2_out = A_B ? not_4_out : 5'bz;  // Controlled_Buffer controlled_buffer_2
  Adder #(.width(5)) adder_2 (.a(controlled_buffer_2_out), .b(in_10), .out(out_20), .cin(in_9));  // open: cout
  Comparator #(.width(5), .mode("unsigned")) comparator_1 (
    .a(out_16), .b(in_11), .gt(comparator_1_gt), .eq(A_B_3), .lt(comparator_1_lt));
  or or_2 (or_2_out, comparator_1_gt, comparator_1_lt);
  Adder #(.width(5)) adder_3 (.a(_20), .b(_9), .out(adder_3_out), .cout(adder_3_cout));  // open: cin
  assign A_B_2 = adder_1_cout ? or_2_out : 1'bz;  // Controlled_Buffer controlled_buffer_3
  // AND_Gate and_1 has open pins: in0=in_7, in1=xor_2_out, out=open
  assign out_13 = or_1_out ? adder_3_out : 5'bz;  // Controlled_Buffer controlled_buffer_4
  xor xor_2 (xor_2_out, As_2, Bs_2);
  not not_6 (not_6_out, undriven);

  assign out_12 = As_2;
  assign out_14 = As;
  assign out_19 = As_2;
  assign out_22 = As;
  assign out_23 = As_2;
  assign out_24 = out_16;
  assign out_26 = out_16;

  // Notes on the sheet:
  //   23CE020
endmodule
