// Logisim project OneDigit7Seg.circ as structural Verilog: 2 circuits, main circuit main
module main (
  input  [3:0] in_1
);

  wire bcd_to_7seg_1_f1, bcd_to_7seg_1_f2, bcd_to_7seg_1_f3, bcd_to_7seg_1_f4, bcd_to_7seg_1_f5,
       bcd_to_7seg_1_f6, bcd_to_7seg_1_f7;

  BCD_to_7Seg bcd_to_7seg_1 (
    .A(in_1[3]), .B(in_1[2]), .C(in_1[1]), .D(in_1[0]), .f1(bcd_to_7seg_1_f1), .f2(bcd_to_7seg_1_f2),
    .f3(bcd_to_7seg_1_f3), .f4(bcd_to_7seg_1_f4), .f5(bcd_to_7seg_1_f5), .f6(bcd_to_7seg_1_f6),
    .f7(bcd_to_7seg_1_f7));
  _7_Segment_Display u_7_segment_display_1 (
    .g(bcd_to_7seg_1_f4), .f(bcd_to_7seg_1_f3), .a(bcd_to_7seg_1_f2), .b(bcd_to_7seg_1_f1),
    .e(bcd_to_7seg_1_f5), .d(bcd_to_7seg_1_f6), .c(bcd_to_7seg_1_f7));  // open: dp

  // Notes on the sheet:
  //   23CE020
endmodule

module BCD_to_7Seg (
  input  A,
  input  B,
  input  C,
  input  D,
  output f1,
  output f2,
  output f3,
  output f4,
  output f5,
  output f6,
  output f7
);

  wire and_1_out, and_2_out, and_3_out, and_4_out, and_5_out, and_6_out, and_7_out, and_8_out, and_9_out,
       and_10_out, and_11_out, and_12_out, and_13_out, and_14_out, and_15_out, and_16_out, not_1_out,
       not_2_out, not_3_out, not_4_out, not_5_out, not_6_out, not_7_out, not_8_out, not_9_out, not_10_out,
       not_11_out, not_12_out, not_13_out, not_14_out, not_15_out, not_16_out, not_17_out, not_18_out,
       not_19_out, not_20_out, not_21_out;

  not not_1 (not_1_out, B);
  not not_2 (not_2_out, C);
  and and_1 (and_1_out, not_2_out, not_3_out);
  not not_3 (not_3_out, D);
  and and_2 (and_2_out, C, D);
  not not_4 (not_4_out, B);
  and and_3 (and_3_out, not_4_out, not_5_out);
  not not_5 (not_5_out, D);
  and and_4 (and_4_out, B, D);
  not not_6 (not_6_out, C);
  and and_5 (and_5_out, not_6_out, not_7_out);
  not not_7 (not_7_out, D);
  and and_6 (and_6_out, B, not_8_out);
  not not_8 (not_8_out, C);
  and and_7 (and_7_out, B, not_9_out);
  not not_9 (not_9_out, D);
  not not_10 (not_10_out, B);
  and and_8 (and_8_out, not_10_out, C);
  and and_9 (and_9_out, B, not_11_out);
  not not_11 (not_11_out, C);
  and and_10 (and_10_out, B, not_12_out);
  not not_12 (not_12_out, D);
  not not_13 (not_13_out, B);
  and and_11 (and_11_out, not_13_out, not_14_out);
  not not_14 (not_14_out, D);
  and and_12 (and_12_out, C, not_15_out);
  not not_15 (not_15_out, D);
  not not_16 (not_16_out, B);
  and and_13 (and_13_out, not_16_out, not_17_out);
  not not_17 (not_17_out, D);
  not not_18 (not_18_out, B);
  and and_14 (and_14_out, not_18_out, C);
  and and_15 (and_15_out, C, not_19_out);
  not not_19 (not_19_out, D);
  and and_16 (and_16_out, B, not_20_out, D);
  not not_20 (not_20_out, C);
  not not_21 (not_21_out, C);
  or or_1 (f7, not_21_out, D, B);
  or or_2 (f1, not_1_out, and_1_out, and_2_out);
  or or_3 (f2, and_3_out, C, and_4_out, A);
  or or_4 (f3, and_5_out, and_6_out, and_7_out, A);
  or or_5 (f4, and_8_out, and_9_out, and_10_out, A);
  or or_6 (f5, and_11_out, and_12_out);
  or or_7 (f6, and_13_out, and_14_out, and_15_out, and_16_out, A);
endmodule
