// Logisim project PRACTICAL_2.circ as structural Verilog
module _7_bit_led_display (
  input  a,
  input  b,
  input  c,
  input  d,
  output A_2,
  output B_2,
  output C_2,
  output D_2,
  output E,
  output F,
  output G
);

  wire and_1_out, and_2_out, and_3_out, and_4_out, and_5_out, and_6_out, and_7_out, and_8_out, and_9_out,
       and_10_out, and_11_out, and_12_out, not_1_out, not_2_out, not_3_out, not_4_out, not_5_out, not_6_out,
       not_7_out, not_8_out, not_9_out, not_10_out, not_11_out, not_12_out, not_13_out, not_14_out,
       not_15_out, not_16_out;

  not not_1 (not_1_out, c);
  and and_1 (and_1_out, not_1_out, not_2_out);
  not not_2 (not_2_out, d);
  and and_2 (and_2_out, b, not_3_out);
  not not_3 (not_3_out, c);
  and and_3 (and_3_out, b, not_4_out);
  not not_4 (not_4_out, d);
  not not_5 (not_5_out, b);
  and and_4 (and_4_out, not_5_out, not_6_out);
  not not_6 (not_6_out, d);
  and and_5 (and_5_out, b, d);
  not not_7 (not_7_out, b);
  and and_6 (and_6_out, c, d);
  or or_1 (D_2, c, b, a);
  not not_8 (not_8_out, c);
  or or_2 (E, not_8_out, d, b);
  not not_9 (not_9_out, b);
  and and_7 (and_7_out, not_9_out, not_10_out);
  not not_10 (not_10_out, d);
  not not_11 (not_11_out, b);
  and and_8 (and_8_out, not_11_out, c);
  and and_9 (and_9_out, c, not_12_out);
  not not_12 (not_12_out, d);
  not not_13 (not_13_out, c);
  and and_10 (and_10_out, b, not_13_out, d);
  not not_14 (not_14_out, b);
  and and_11 (and_11_out, not_14_out, not_15_out);
  not not_15 (not_15_out, d);
  and and_12 (and_12_out, c, not_16_out);
  not not_16 (not_16_out, d);
  or or_3 (A_2, and_1_out, and_2_out, and_3_out);
  or or_4 (B_2, and_4_out, c, and_5_out);
  or or_5 (C_2, not_7_out, and_6_out);
  or or_6 (F, and_7_out, and_8_out, and_9_out, and_10_out);
  or or_7 (G, and_11_out, and_12_out);
endmodule
