// Logisim project TwoDigit7Seg.circ as structural Verilog: 2 circuits, main circuit main
module main (
  input  [6:0] Binary
);

  wire BCD_to_7seg_2_f1, BCD_to_7seg_2_f2, BCD_to_7seg_2_f3, BCD_to_7seg_2_f4, BCD_to_7seg_2_f5,
       BCD_to_7seg_2_f6, BCD_to_7seg_2_f7, BCD_to_7seg_f1, BCD_to_7seg_f2, BCD_to_7seg_f3, BCD_to_7seg_f4,
       BCD_to_7seg_f5, BCD_to_7seg_f6, BCD_to_7seg_f7, Bnary_to_BCD_o1, Bnary_to_BCD_o2, Bnary_to_BCD_o3,
       Bnary_to_BCD_o4, Bnary_to_BCD_t1, Bnary_to_BCD_t2, Bnary_to_BCD_t3, Bnary_to_BCD_t4;

  BinaryToBCD Bnary_to_BCD (
    .A(Binary[6]), .B(Binary[5]), .C(Binary[4]), .D(Binary[3]), .E(Binary[2]), .F(Binary[1]), .G(Binary[0]),
    .t1(Bnary_to_BCD_t1), .t2(Bnary_to_BCD_t2), .t3(Bnary_to_BCD_t3), .t4(Bnary_to_BCD_t4),
    .o1(Bnary_to_BCD_o1), .o2(Bnary_to_BCD_o2), .o3(Bnary_to_BCD_o3), .o4(Bnary_to_BCD_o4));
  BCD_to_7Seg BCD_to_7seg (
    .A(Bnary_to_BCD_t1), .B(Bnary_to_BCD_t2), .C(Bnary_to_BCD_t3), .D(Bnary_to_BCD_t4), .f1(BCD_to_7seg_f1),
    .f2(BCD_to_7seg_f2), .f3(BCD_to_7seg_f3), .f4(BCD_to_7seg_f4), .f5(BCD_to_7seg_f5), .f6(BCD_to_7seg_f6),
    .f7(BCD_to_7seg_f7));
  BCD_to_7Seg BCD_to_7seg_2 (
    .A(Bnary_to_BCD_o1), .B(Bnary_to_BCD_o2), .C(Bnary_to_BCD_o3), .D(Bnary_to_BCD_o4),
    .f1(BCD_to_7seg_2_f1), .f2(BCD_to_7seg_2_f2), .f3(BCD_to_7seg_2_f3), .f4(BCD_to_7seg_2_f4),
    .f5(BCD_to_7seg_2_f5), .f6(BCD_to_7seg_2_f6), .f7(BCD_to_7seg_2_f7));
  _7_Segment_Display u_7_segment_display_1 (
    .g(BCD_to_7seg_f4), .f(BCD_to_7seg_f3), .a(BCD_to_7seg_f2), .b(BCD_to_7seg_f1), .e(BCD_to_7seg_f5),
    .d(BCD_to_7seg_f6), .c(BCD_to_7seg_f7));  // open: dp
  _7_Segment_Display u_7_segment_display_2 (
    .g(BCD_to_7seg_2_f4), .f(BCD_to_7seg_2_f3), .a(BCD_to_7seg_2_f2), .b(BCD_to_7seg_2_f1),
    .e(BCD_to_7seg_2_f5), .d(BCD_to_7seg_2_f6), .c(BCD_to_7seg_2_f7));  // open: dp

  // Notes on the sheet:
  //   23CE020
endmodule

module BinaryToBCD (
  input  A,
  input  B,
  input  C,
  input  D,
  input  E,
  input  F,
  input  G,
  output t1,
  output t2,
  output t3,
  output t4,
  output o1,
  output o2,
  output o3,
  output o4
);

  wire and_1_out, and_2_out, and_3_out, and_4_out, and_5_out, and_6_out, and_7_out, and_8_out, and_9_out,
       and_10_out, and_11_out, and_12_out, and_13_out, and_14_out, and_15_out, and_16_out, and_17_out,
       and_18_out, and_19_out, and_20_out, and_21_out, and_22_out, and_23_out, and_24_out, and_25_out,
       and_26_out, and_27_out, and_28_out, and_29_out, and_30_out, and_31_out, and_32_out, and_33_out,
       and_34_out, and_35_out, and_36_out, and_37_out, and_38_out, and_39_out, and_40_out, and_41_out,
       and_42_out, and_43_out, and_44_out, and_45_out, and_46_out, and_47_out, and_48_out, and_49_out,
       and_50_out, and_51_out, and_52_out, and_53_out, and_54_out, and_55_out, and_56_out, and_57_out,
       and_58_out, not_1_out, not_2_out, not_3_out, not_4_out, not_5_out, not_6_out, not_7_out, not_8_out,
       not_9_out, not_10_out, not_11_out, not_12_out, not_13_out, not_14_out, not_15_out, not_16_out,
       not_17_out, not_18_out, not_19_out, not_20_out, not_21_out, not_22_out, not_23_out, not_24_out,
       not_25_out, not_26_out, not_27_out, not_28_out, not_29_out, not_30_out, not_31_out, not_32_out,
       not_33_out, not_34_out, not_35_out, not_36_out, not_37_out, not_38_out, not_39_out, not_40_out,
       not_41_out, not_42_out, not_43_out, not_44_out, not_45_out, not_46_out, not_47_out, not_48_out,
       not_49_out, not_50_out, not_51_out, not_52_out, not_53_out, not_54_out, not_55_out, not_56_out,
       not_57_out, not_58_out, not_59_out, not_60_out, not_61_out, not_62_out, not_63_out, not_64_out,
       not_65_out, not_66_out, not_67_out, not_68_out, not_69_out, not_70_out, not_71_out, not_72_out,
       not_73_out, not_74_out, not_75_out, not_76_out, not_77_out, not_78_out, not_79_out, not_80_out,
       not_81_out, not_82_out, not_83_out, not_84_out, not_85_out, not_86_out, not_87_out, not_88_out,
       not_89_out, not_90_out, not_91_out, not_92_out, not_93_out, not_94_out, not_95_out, not_96_out,
       not_97_out, not_98_out, not_99_out, not_100_out, not_101_out, not_102_out, not_103_out, not_104_out,
       not_105_out, not_106_out, not_107_out, not_108_out, not_109_out, not_110_out, not_111_out,
       not_112_out, not_113_out, not_114_out, not_115_out;

  and and_1 (and_1_out, A, C);
  and and_2 (and_2_out, A, B);
  not not_1 (not_1_out, B);
  not not_2 (not_2_out, C);
  not not_3 (not_3_out, A);
  not not_4 (not_4_out, B);
  not not_5 (not_5_out, A);
  not not_6 (not_6_out, B);
  not not_7 (not_7_out, A);
  not not_8 (not_8_out, A);
  not not_9 (not_9_out, C);
  not not_10 (not_10_out, D);
  not not_11 (not_11_out, B);
  not not_12 (not_12_out, C);
  not not_13 (not_13_out, B);
  not not_14 (not_14_out, C);
  not not_15 (not_15_out, B);
  not not_16 (not_16_out, C);
  not not_17 (not_17_out, B);
  not not_18 (not_18_out, A);
  not not_19 (not_19_out, B);
  not not_20 (not_20_out, D);
  not not_21 (not_21_out, E);
  not not_22 (not_22_out, C);
  not not_23 (not_23_out, D);
  not not_24 (not_24_out, D);
  not not_25 (not_25_out, D);
  not not_26 (not_26_out, E);
  not not_27 (not_27_out, C);
  not not_28 (not_28_out, C);
  not not_29 (not_29_out, A);
  not not_30 (not_30_out, B);
  not not_31 (not_31_out, C);
  not not_32 (not_32_out, E);
  not not_33 (not_33_out, F);
  not not_34 (not_34_out, A);
  not not_35 (not_35_out, B);
  not not_36 (not_36_out, D);
  not not_37 (not_37_out, E);
  not not_38 (not_38_out, A);
  not not_39 (not_39_out, B);
  not not_40 (not_40_out, F);
  not not_41 (not_41_out, C);
  not not_42 (not_42_out, D);
  not not_43 (not_43_out, D);
  not not_44 (not_44_out, E);
  not not_45 (not_45_out, F);
  not not_46 (not_46_out, E);
  not not_47 (not_47_out, C);
  not not_48 (not_48_out, D);
  not not_49 (not_49_out, F);
  not not_50 (not_50_out, C);
  not not_51 (not_51_out, E);
  not not_52 (not_52_out, F);
  not not_53 (not_53_out, A);
  not not_54 (not_54_out, B);
  not not_55 (not_55_out, C);
  not not_56 (not_56_out, D);
  not not_57 (not_57_out, A);
  not not_58 (not_58_out, C);
  not not_59 (not_59_out, A);
  not not_60 (not_60_out, B);
  not not_61 (not_61_out, E);
  not not_62 (not_62_out, F);
  not not_63 (not_63_out, A);
  not not_64 (not_64_out, B);
  not not_65 (not_65_out, E);
  not not_66 (not_66_out, A);
  not not_67 (not_67_out, E);
  not not_68 (not_68_out, F);
  not not_69 (not_69_out, A);
  not not_70 (not_70_out, C);
  not not_71 (not_71_out, D);
  not not_72 (not_72_out, E);
  not not_73 (not_73_out, C);
  not not_74 (not_74_out, F);
  not not_75 (not_75_out, D);
  not not_76 (not_76_out, C);
  not not_77 (not_77_out, D);
  not not_78 (not_78_out, E);
  not not_79 (not_79_out, F);
  not not_80 (not_80_out, B);
  not not_81 (not_81_out, C);
  not not_82 (not_82_out, E);
  not not_83 (not_83_out, C);
  not not_84 (not_84_out, F);
  not not_85 (not_85_out, D);
  not not_86 (not_86_out, B);
  not not_87 (not_87_out, C);
  not not_88 (not_88_out, D);
  not not_89 (not_89_out, E);
  not not_90 (not_90_out, A);
  not not_91 (not_91_out, B);
  not not_92 (not_92_out, D);
  not not_93 (not_93_out, B);
  not not_94 (not_94_out, C);
  not not_95 (not_95_out, F);
  not not_96 (not_96_out, A);
  not not_97 (not_97_out, B);
  not not_98 (not_98_out, D);
  not not_99 (not_99_out, E);
  not not_100 (not_100_out, F);
  not not_101 (not_101_out, A);
  not not_102 (not_102_out, B);
  not not_103 (not_103_out, E);
  not not_104 (not_104_out, C);
  not not_105 (not_105_out, D);
  not not_106 (not_106_out, F);
  not not_107 (not_107_out, D);
  not not_108 (not_108_out, F);
  not not_109 (not_109_out, C);
  not not_110 (not_110_out, E);
  not not_111 (not_111_out, F);
  not not_112 (not_112_out, C);
  not not_113 (not_113_out, F);
  not not_114 (not_114_out, F);
  not not_115 (not_115_out, D);
  or or_1 (t1, and_1_out, and_2_out);
  and and_3 (and_3_out, B, D);
  and and_4 (and_4_out, B, C);
  and and_5 (and_5_out, A, not_1_out, not_2_out);
  and and_6 (and_6_out, not_3_out, not_4_out, C, E);
  and and_7 (and_7_out, not_5_out, not_6_out, C, D);
  and and_8 (and_8_out, not_7_out, C, D, E);
  and and_9 (and_9_out, not_8_out, B, not_9_out, not_10_out);
  and and_10 (and_10_out, A, not_11_out, not_12_out);
  and and_11 (and_11_out, not_13_out, not_14_out, D, F);
  and and_12 (and_12_out, not_15_out, not_16_out, D, E);
  and and_13 (and_13_out, not_17_out, D, E, F);
  and and_14 (and_14_out, not_18_out, not_19_out, C, not_20_out, not_21_out);
  and and_15 (and_15_out, B, not_22_out, not_23_out);
  and and_16 (and_16_out, B, not_24_out, F);
  and and_17 (and_17_out, B, not_25_out, E);
  and and_18 (and_18_out, B, C, D, not_26_out);
  and and_19 (and_19_out, A, not_27_out, E, F);
  and and_20 (and_20_out, A, not_28_out, D);
  and and_21 (and_21_out, A, D, F);
  and and_22 (and_22_out, A, D, E);
  and and_23 (and_23_out, not_29_out, not_30_out, not_31_out, D, not_32_out, not_33_out);
  and and_24 (and_24_out, not_34_out, not_35_out, C, not_36_out, not_37_out, F);
  and and_25 (and_25_out, not_38_out, not_39_out, C, D, E, not_40_out);
  and and_26 (and_26_out, B, not_41_out, not_42_out, E, F);
  and and_27 (and_27_out, B, C, not_43_out, not_44_out, not_45_out);
  and and_28 (and_28_out, B, C, D, not_46_out, F);
  and and_29 (and_29_out, A, not_47_out, not_48_out, E, not_49_out);
  and and_30 (and_30_out, A, not_50_out, D, E, F);
  and and_31 (and_31_out, A, C, D, not_51_out, not_52_out);
  and and_32 (and_32_out, A, B, F);
  and and_33 (and_33_out, not_53_out, not_54_out, not_55_out, not_56_out, E);
  and and_34 (and_34_out, not_57_out, not_58_out, D, E, F);
  and and_35 (and_35_out, not_59_out, not_60_out, C, not_61_out, not_62_out);
  and and_36 (and_36_out, not_63_out, not_64_out, C, D, not_65_out);
  and and_37 (and_37_out, not_66_out, C, D, not_67_out, not_68_out);
  and and_38 (and_38_out, not_69_out, B, not_70_out, not_71_out, not_72_out, F);
  and and_39 (and_39_out, B, not_73_out, E, not_74_out);
  and and_40 (and_40_out, B, C, not_75_out, E, F);
  and and_41 (and_41_out, A, not_76_out, not_77_out, not_78_out, not_79_out);
  and and_42 (and_42_out, A, not_80_out, not_81_out, not_82_out, F);
  and and_43 (and_43_out, A, not_83_out, D, E, not_84_out);
  and and_44 (and_44_out, A, C, not_85_out, E);
  and and_45 (and_45_out, A, C, E, F);
  and and_46 (and_46_out, not_86_out, not_87_out, not_88_out, not_89_out, F);
  and and_47 (and_47_out, not_90_out, not_91_out, not_92_out, E, F);
  and and_48 (and_48_out, not_93_out, not_94_out, D, E, not_95_out);
  and and_49 (and_49_out, not_96_out, not_97_out, C, not_98_out, not_99_out, not_100_out);
  and and_50 (and_50_out, not_101_out, not_102_out, C, D, not_103_out, F);
  and and_51 (and_51_out, B, not_104_out, not_105_out, not_106_out);
  and and_52 (and_52_out, B, not_107_out, E, not_108_out);
  and and_53 (and_53_out, B, not_109_out, D, F);
  and and_54 (and_54_out, B, D, E, F);
  and and_55 (and_55_out, B, C, D, not_110_out, not_111_out);
  and and_56 (and_56_out, A, not_112_out, D, not_113_out);
  and and_57 (and_57_out, A, D, E, not_114_out);
  and and_58 (and_58_out, A, C, not_115_out, F);
  or or_2 (t2, and_3_out, and_4_out, and_5_out);
  or or_3 (t3, and_6_out, and_7_out, and_8_out, and_9_out, and_10_out);
  or or_4 (t4, and_11_out, and_12_out, and_13_out, and_14_out, and_15_out, and_16_out, and_17_out, and_18_out, and_19_out, and_20_out, and_21_out, and_22_out);
  or or_5 (o1, and_23_out, and_24_out, and_25_out, and_26_out, and_27_out, and_28_out, and_29_out, and_30_out, and_31_out, and_32_out);
  or or_6 (o2, and_33_out, and_34_out, and_35_out, and_36_out, and_37_out, and_38_out, and_39_out, and_40_out, and_41_out, and_42_out, and_43_out, and_44_out, and_45_out);
  or or_7 (o3, and_46_out, and_47_out, and_48_out, and_49_out, and_50_out, and_51_out, and_52_out, and_53_out, and_54_out, and_55_out, and_56_out, and_57_out, and_58_out);

  assign o4 = G;
endmodule
