// Logisim project coa-pra-6.circ as structural Verilog: 1 circuit, main circuit main
module main (
  input  in_1,
  input  in_2,
  input  in_3,
  input  in_4,
  input  in_5,
  input  in_6,
  input  in_7,
  input  in_8,
  input  in_9,
  input  in_10,
  input  in_11,
  input  in_12,
  input  in_13,
  input  in_14,
  input  in_15,
  input  in_16,
  input  in_17,
  input  in_18,
  input  in_19,
  input  in_20,
  input  in_21,
  output out_22,
  output out_23,
  output out_24,
  output out_25,
  output out_26,
  output out_27,
  output out_28,
  output out_29,
  output out_30,
  output out_31,
  output out_32,
  output out_33
);

  Multiplexer multiplexer_1 (.in0(in_5), .in1(in_2), .out(out_22), .sel(in_7), .en(in_8));
  Multiplexer multiplexer_2 (.in0(in_9), .in1(in_10), .out(out_26), .sel(in_18), .en(in_20));
  Multiplexer multiplexer_3 (.in0(in_1), .in1(in_3), .out(out_23), .sel(in_7), .en(in_8));
  Multiplexer multiplexer_4 (.in0(in_9), .in1(in_11), .out(out_27), .sel(in_18), .en(in_20));
  Multiplexer multiplexer_5 (.in0(in_2), .in1(in_4), .out(out_24), .sel(in_7), .en(in_8));
  Multiplexer multiplexer_6 (.in0(in_10), .in1(in_12), .out(out_28), .sel(in_18), .en(in_20));
  Multiplexer multiplexer_7 (.in0(in_11), .in1(in_17), .out(out_29), .sel(in_18), .en(in_20));
  Multiplexer multiplexer_8 (.in0(in_3), .in1(in_6), .out(out_25), .sel(in_7), .en(in_8));
  Multiplexer multiplexer_9 (.in0(in_16), .in1(in_14), .out(out_30), .sel(in_19), .en(in_21));
  Multiplexer multiplexer_10 (.in0(in_13), .in1(in_15), .out(out_31), .sel(in_19), .en(in_21));
  Multiplexer multiplexer_11 (.in0(in_14), .in1(in_16), .out(out_32), .sel(in_19), .en(in_21));
  Multiplexer multiplexer_12 (.in0(in_15), .in1(in_13), .out(out_33), .sel(in_19), .en(in_21));

  // Notes on the sheet:
  //   23CE021
  //   23CE021
  //   23CE021
endmodule
