// Logisim project coa-pract-5.circ as structural Verilog: 1 circuit, main circuit main
module main (
  input  [3:0] in_1,
  input  [3:0] in_2,
  input  [3:0] in_3,
  input  [3:0] in_4,
  input  in_5,
  input  [1:0] in_6,
  output [3:0] out_7
);

  wire clock_1_out, decoder_1_out0, decoder_1_out1, decoder_1_out2, decoder_1_out3;
  wire [3:0] register_1_q, register_2_q, register_3_q, register_4_q;

  Clock clock_1 (.out(clock_1_out));
  Decoder #(.select(2)) decoder_1 (
    .out0(decoder_1_out0), .out1(decoder_1_out1), .out2(decoder_1_out2), .out3(decoder_1_out3), .sel(in_6),
    .en(in_5));
  Register #(.width(4)) register_1 (.D(in_1), .en(in_5), .Q(register_1_q), .clk(clock_1_out));  // open: clr
  assign out_7 = decoder_1_out0 ? register_1_q : 4'bz;  // Controlled_Buffer controlled_buffer_1
  Register #(.width(4)) register_2 (.D(in_2), .en(in_5), .Q(register_2_q), .clk(clock_1_out));  // open: clr
  assign out_7 = decoder_1_out1 ? register_2_q : 4'bz;  // Controlled_Buffer controlled_buffer_2
  Register #(.width(4)) register_3 (.D(in_3), .en(in_5), .Q(register_3_q), .clk(clock_1_out));  // open: clr
  assign out_7 = decoder_1_out2 ? register_3_q : 4'bz;  // Controlled_Buffer controlled_buffer_3
  Register #(.width(4)) register_4 (.D(in_4), .en(in_5), .Q(register_4_q), .clk(clock_1_out));  // open: clr
  assign out_7 = decoder_1_out3 ? register_4_q : 4'bz;  // Controlled_Buffer controlled_buffer_4

  // Notes on the sheet:
  //   23CE012
endmodule
