// Logisim project coa_prac_3.circ as structural Verilog: 1 circuit, main circuit main
module main (
  input  in_1,
  input  B0,
  input  A0,
  input  B1,
  input  A1,
  input  B2,
  input  A2,
  input  B3,
  input  A3,
  input  in_10,
  input  [1:0] in_11,
  input  [4:0] A,
  input  [4:0] B,
  input  [1:0] in_14,
  output D0,
  output D1,
  output D2,
  output D3,
  output out_19,
  output [4:0] out_20
);

  wire adder_1_cout, adder_2_cout, adder_3_cout, multiplexer_1_out, multiplexer_2_out, multiplexer_3_out,
       multiplexer_4_out, not_1_out, not_2_out, not_3_out, not_4_out, not_5_out;
  wire [4:0] and_1_out, not_6_out, or_1_out, xor_1_out;

  not not_1 (not_1_out, B0);
  not not_2 (not_2_out, B1);
  not not_3 (not_3_out, B2);
  not not_4 (not_4_out, B3);
  Multiplexer #(.select(2)) multiplexer_1 (
    .in0(B0), .in1(not_1_out), .in2(in_10), .in3(not_5_out), .out(multiplexer_1_out), .sel(in_11), .en(1'b1));
  Multiplexer #(.select(2)) multiplexer_2 (
    .in0(B1), .in1(not_2_out), .in2(in_10), .in3(not_5_out), .out(multiplexer_2_out), .sel(in_11), .en(1'b1));
  Multiplexer #(.select(2)) multiplexer_3 (
    .in0(B2), .in1(not_3_out), .in2(in_10), .in3(not_5_out), .out(multiplexer_3_out), .sel(in_11), .en(1'b1));
  Multiplexer #(.select(2)) multiplexer_4 (
    .in0(B3), .in1(not_4_out), .in2(in_10), .in3(not_5_out), .out(multiplexer_4_out), .sel(in_11), .en(1'b1));
  not not_5 (not_5_out, in_10);
  assign and_1_out = A & B;  // AND_Gate and_1, 5 bits wide
  assign or_1_out = A | B;  // OR_Gate or_1, 5 bits wide
  assign xor_1_out = A ^ B;  // XOR_Gate xor_1, 5 bits wide
  assign not_6_out = ~A;  // NOT_Gate not_6, 5 bits wide
  Adder #(.width(1)) adder_1 (.a(A0), .b(multiplexer_1_out), .out(D0), .cin(in_1), .cout(adder_1_cout));
  Adder #(.width(1)) adder_2 (.a(A1), .b(multiplexer_2_out), .out(D1), .cin(adder_1_cout), .cout(adder_2_cout));
  Adder #(.width(1)) adder_3 (.a(A2), .b(multiplexer_3_out), .out(D2), .cin(adder_2_cout), .cout(adder_3_cout));
  Adder #(.width(1)) adder_4 (.a(A3), .b(multiplexer_4_out), .out(D3), .cin(adder_3_cout), .cout(out_19));
  Multiplexer #(.select(2), .width(5)) multiplexer_5 (
    .in0(and_1_out), .in1(or_1_out), .in2(xor_1_out), .in3(not_6_out), .out(out_20), .sel(in_14), .en(1'b1));

  // Notes on the sheet:
  //   23CE012
  //   23CE012
endmodule
