// Logisim project coa_practical_4.circ as structural Verilog: 1 circuit, main circuit main
module main (
  input  [1:0] in_1,
  input  in_2,
  input  in_3,
  input  [3:0] R,
  input  [3:0] in_5,
  input  [3:0] in_6,
  input  [3:0] in_7,
  output [3:0] out_8
);

  wire clock_1_out;
  wire [3:0] register_1_q, register_2_q, register_3_q, register_4_q;

  Clock clock_1 (.out(clock_1_out));
  Register #(.width(4)) register_1 (.D(R), .en(in_3), .Q(register_1_q), .clk(clock_1_out), .clr(in_2));
  Register #(.width(4)) register_2 (.D(in_5), .en(in_3), .Q(register_2_q), .clk(clock_1_out), .clr(in_2));
  Multiplexer #(.select(2), .width(4)) multiplexer_1 (
    .in0(register_1_q), .in1(register_2_q), .in2(register_3_q), .in3(register_4_q), .out(out_8), .sel(in_1),
    .en(in_3));
  Register #(.width(4)) register_3 (.D(in_6), .en(in_3), .Q(register_3_q), .clk(clock_1_out), .clr(in_2));
  Register #(.width(4)) register_4 (.D(in_7), .en(in_3), .Q(register_4_q), .clk(clock_1_out), .clr(in_2));

  // Notes on the sheet:
  //   23CE012
endmodule
