// Logisim project exp1_23CE004.circ as structural Verilog
module BCD_To_7Seg (
  input  A,
  input  B,
  input  C,
  input  D,
  output a_2,
  output b_2,
  output c_2,
  output d_2,
  output e,
  output f,
  output g
);

  wire and_1_out, and_2_out, and_3_out, and_4_out, and_5_out, and_6_out, and_7_out, and_8_out, and_9_out,
       and_10_out, and_11_out, and_12_out, nand_1_out, nand_2_out, nand_3_out, nand_4_out, nand_5_out,
       nand_6_out, nand_7_out, nand_8_out, nand_9_out, nand_10_out, nand_11_out, nand_12_out, nand_13_out,
       nand_14_out, nand_15_out, nand_16_out, nand_17_out, nand_18_out, nand_19_out, nand_20_out,
       nand_21_out, nand_22_out, nand_23_out, nand_24_out, nand_25_out, nand_26_out, nand_27_out,
       nand_28_out, nand_29_out, nand_30_out, nand_31_out, nand_32_out, nand_33_out, nand_34_out,
       nand_35_out, nand_36_out, nand_37_out, nand_38_out, nand_39_out, nand_41_out, nand_42_out, nand_43_out;

  nand nand_1 (nand_1_out, B, B);
  nand nand_2 (nand_2_out, D, D);
  nand nand_3 (nand_3_out, C, C);
  nand nand_4 (nand_4_out, D, D);
  nand nand_5 (nand_5_out, D, D);
  nand nand_6 (nand_6_out, B, B);
  nand nand_7 (nand_7_out, D, D);
  nand nand_8 (nand_8_out, B, B);
  nand nand_9 (nand_9_out, C, C);
  nand nand_10 (nand_10_out, B, B);
  nand nand_11 (nand_11_out, D, D);
  nand nand_12 (nand_12_out, D, D);
  nand nand_13 (nand_13_out, C, C);
  nand nand_14 (nand_14_out, D, D);
  nand nand_15 (nand_15_out, C, C);
  nand nand_16 (nand_16_out, D, D);
  nand nand_17 (nand_17_out, B, B);
  nand nand_18 (nand_18_out, C, C);
  nand nand_19 (nand_19_out, D, D);
  nand nand_20 (nand_20_out, nand_1_out, nand_2_out);
  nand nand_21 (nand_21_out, C, C);
  nand nand_22 (nand_22_out, B, D);
  nand nand_23 (nand_23_out, A, A);
  nand nand_24 (nand_24_out, nand_3_out, nand_4_out);
  and and_1 (and_1_out, C, nand_5_out);
  nand nand_25 (nand_25_out, B, B);
  nand nand_26 (nand_26_out, nand_6_out, nand_7_out);
  nand nand_27 (nand_27_out, nand_8_out, C);
  nand nand_28 (nand_28_out, D, D);
  and and_2 (and_2_out, B, nand_9_out);
  nand nand_29 (nand_29_out, nand_10_out, nand_11_out);
  nand nand_30 (nand_30_out, C, nand_12_out);
  nand nand_31 (nand_31_out, nand_13_out, nand_14_out);
  nand nand_32 (nand_32_out, B, nand_15_out);
  nand nand_33 (nand_33_out, B, nand_16_out);
  nand nand_34 (nand_34_out, A, A);
  nand nand_35 (nand_35_out, nand_17_out, C);
  nand nand_36 (nand_36_out, B, nand_18_out);
  nand nand_37 (nand_37_out, B, nand_19_out);
  nand nand_38 (nand_38_out, A, A);
  and and_3 (and_3_out, nand_20_out, nand_21_out);
  and and_4 (and_4_out, nand_22_out, nand_23_out);
  and and_5 (and_5_out, B, nand_24_out);
  nand nand_39 (nand_39_out, C, D);
  nand nand_40 (c_2, and_1_out, nand_25_out);
  and and_6 (and_6_out, nand_26_out, nand_27_out);
  nand nand_41 (nand_41_out, C, nand_28_out);
  nand nand_42 (nand_42_out, and_2_out, D);
  nand nand_43 (nand_43_out, A, A);
  nand nand_44 (e, nand_29_out, nand_30_out);
  and and_7 (and_7_out, nand_31_out, nand_32_out);
  and and_8 (and_8_out, nand_33_out, nand_34_out);
  and and_9 (and_9_out, nand_35_out, nand_36_out);
  and and_10 (and_10_out, nand_37_out, nand_38_out);
  nand nand_45 (a_2, and_3_out, and_4_out);
  nand nand_46 (b_2, and_5_out, nand_39_out);
  and and_11 (and_11_out, and_6_out, nand_41_out);
  and and_12 (and_12_out, nand_42_out, nand_43_out);
  nand nand_47 (f, and_7_out, and_8_out);
  nand nand_48 (g, and_9_out, and_10_out);
  nand nand_49 (d_2, and_11_out, and_12_out);

  // Notes on the sheet:
  //   23CE004
endmodule

module _7Seg_0_to_9 (
  input  [3:0] in_1
);

  wire bcd_to_7seg_1_a_2, bcd_to_7seg_1_b_2, bcd_to_7seg_1_c_2, bcd_to_7seg_1_d_2, bcd_to_7seg_1_e,
       bcd_to_7seg_1_f, bcd_to_7seg_1_g;

  BCD_To_7Seg bcd_to_7seg_1 (
    .A(in_1[3]), .B(in_1[2]), .C(in_1[1]), .D(in_1[0]), .a_2(bcd_to_7seg_1_a_2), .b_2(bcd_to_7seg_1_b_2),
    .c_2(bcd_to_7seg_1_c_2), .d_2(bcd_to_7seg_1_d_2), .e(bcd_to_7seg_1_e), .f(bcd_to_7seg_1_f),
    .g(bcd_to_7seg_1_g));
  _7_Segment_Display u_7_segment_display_1 (
    .g(bcd_to_7seg_1_g), .f(bcd_to_7seg_1_f), .a(bcd_to_7seg_1_a_2), .b(bcd_to_7seg_1_b_2),
    .e(bcd_to_7seg_1_e), .d(bcd_to_7seg_1_d_2), .c(bcd_to_7seg_1_c_2));  // open: dp
endmodule

module _7Bit_to_BCD (
  input  A,
  input  B,
  input  C,
  input  D,
  input  E,
  input  F,
  input  G,
  output a_2,
  output b_2,
  output c_2,
  output d_2,
  output e_2,
  output f_2,
  output g_2,
  output h
);

  wire and_1_out, and_2_out, and_3_out, and_4_out, and_5_out, and_6_out, and_7_out, and_8_out, and_9_out,
       and_10_out, and_11_out, and_12_out, and_13_out, and_14_out, and_15_out, and_16_out, and_17_out,
       and_18_out, and_19_out, and_20_out, and_21_out, and_22_out, and_23_out, and_24_out, and_25_out,
       and_26_out, and_27_out, and_28_out, and_29_out, and_30_out, and_31_out, and_32_out, and_33_out,
       and_34_out, and_35_out, and_36_out, and_37_out, and_38_out, and_39_out, and_40_out, and_41_out,
       and_42_out, and_43_out, and_44_out, and_45_out, and_46_out, and_47_out, and_48_out, and_49_out,
       and_50_out, and_51_out, and_52_out, and_53_out, and_54_out, and_55_out, and_56_out, and_57_out,
       and_58_out, and_59_out, and_60_out, and_61_out, and_62_out, and_63_out, and_64_out, and_65_out,
       and_66_out, and_67_out, and_68_out, and_69_out, and_70_out, and_71_out, and_72_out, and_73_out,
       and_74_out, and_75_out, and_76_out, and_77_out, and_78_out, and_79_out, and_80_out, and_81_out,
       and_82_out, and_83_out, and_84_out, and_85_out, and_86_out, and_87_out, and_88_out, and_89_out,
       and_90_out, and_91_out, and_92_out, and_93_out, and_94_out, and_95_out, and_96_out, and_97_out,
       and_98_out, and_99_out, and_100_out, and_101_out, and_102_out, and_103_out, and_104_out, and_105_out,
       and_106_out, and_107_out, and_108_out, and_109_out, and_110_out, and_111_out, and_112_out,
       and_113_out, and_114_out, and_115_out, and_116_out, and_117_out, and_118_out, and_119_out,
       and_120_out, and_121_out, and_122_out, and_123_out, and_124_out, and_125_out, and_126_out,
       and_127_out, and_128_out, and_129_out, and_130_out, and_131_out, and_132_out, and_133_out,
       and_134_out, and_135_out, and_136_out, and_137_out, and_138_out, and_139_out, and_140_out,
       and_141_out, and_142_out, and_143_out, and_144_out, and_145_out, and_146_out, and_147_out,
       and_148_out, and_149_out, and_150_out, and_151_out, and_152_out, and_153_out, and_154_out,
       and_155_out, and_156_out, and_157_out, and_158_out, and_159_out, and_160_out, and_161_out,
       and_162_out, and_163_out, and_164_out, and_165_out, and_166_out, and_167_out, and_168_out,
       and_169_out, and_170_out, and_171_out, and_172_out, and_173_out, and_174_out, and_175_out,
       and_176_out, and_177_out, and_178_out, and_179_out, and_180_out, and_181_out, and_182_out,
       and_183_out, and_184_out, and_185_out, and_186_out, and_187_out, and_188_out, and_189_out, not_1_out,
       not_2_out, not_3_out, not_4_out, not_5_out, not_6_out, not_7_out, not_8_out, not_9_out, not_10_out,
       not_11_out, not_12_out, not_13_out, not_14_out, not_15_out, not_16_out, not_17_out, not_18_out,
       not_19_out, not_20_out, not_21_out, not_22_out, not_23_out, not_24_out, not_25_out, not_26_out,
       not_27_out, not_28_out, not_29_out, not_30_out, not_31_out, not_32_out, not_33_out, not_34_out,
       not_35_out, not_36_out, not_37_out, not_38_out, not_39_out, not_40_out, not_41_out, not_42_out,
       not_43_out, not_44_out, not_45_out, not_46_out, not_47_out, not_48_out, not_49_out, not_50_out,
       not_51_out, not_52_out, not_53_out, not_54_out, not_55_out, not_56_out, not_57_out, not_58_out,
       not_59_out, not_60_out, not_61_out, not_62_out, not_63_out, not_64_out, not_65_out, not_66_out,
       not_67_out, not_68_out, not_69_out, not_70_out, not_71_out, not_72_out, not_73_out, not_74_out,
       not_75_out, not_76_out, not_77_out, not_78_out, not_79_out, not_80_out, not_81_out, not_82_out,
       not_83_out, not_84_out, not_85_out, not_86_out, not_87_out, not_88_out, not_89_out, not_90_out,
       not_91_out, not_92_out, not_93_out, not_94_out, not_95_out, not_96_out, not_97_out, not_98_out,
       not_99_out, not_100_out, not_101_out, not_102_out, not_103_out, not_104_out, not_105_out, not_106_out,
       not_107_out, not_108_out, not_109_out, not_110_out, not_111_out, not_112_out, not_113_out,
       not_114_out, not_115_out, or_2_out, or_4_out, or_5_out, or_6_out, or_7_out, or_8_out, or_9_out,
       or_10_out, or_11_out, or_12_out, or_13_out, or_14_out, or_15_out, or_16_out, or_17_out, or_18_out,
       or_19_out, or_20_out, or_21_out, or_22_out, or_24_out, or_25_out, or_26_out, or_27_out, or_28_out,
       or_29_out, or_30_out, or_31_out, or_32_out, or_33_out, or_34_out, or_35_out, or_36_out, or_37_out,
       or_38_out, or_39_out, or_40_out, or_42_out, or_43_out, or_45_out, or_46_out, or_48_out, or_49_out,
       or_51_out;

  and and_1 (and_1_out, A, C);
  and and_2 (and_2_out, A, B);
  not not_1 (not_1_out, B);
  not not_2 (not_2_out, A);
  not not_3 (not_3_out, B);
  not not_4 (not_4_out, A);
  not not_5 (not_5_out, B);
  not not_6 (not_6_out, A);
  not not_7 (not_7_out, B);
  not not_8 (not_8_out, A);
  not not_9 (not_9_out, B);
  not not_10 (not_10_out, E);
  not not_11 (not_11_out, A);
  not not_12 (not_12_out, B);
  not not_13 (not_13_out, D);
  not not_14 (not_14_out, E);
  not not_15 (not_15_out, C);
  not not_16 (not_16_out, A);
  not not_17 (not_17_out, B);
  not not_18 (not_18_out, A);
  not not_19 (not_19_out, C);
  not not_20 (not_20_out, A);
  not not_21 (not_21_out, B);
  not not_22 (not_22_out, A);
  not not_23 (not_23_out, B);
  not not_24 (not_24_out, A);
  not not_25 (not_25_out, A);
  not not_26 (not_26_out, D);
  not not_27 (not_27_out, E);
  not not_28 (not_28_out, C);
  not not_29 (not_29_out, C);
  not not_30 (not_30_out, B);
  not not_31 (not_31_out, C);
  not not_32 (not_32_out, A);
  not not_33 (not_33_out, B);
  not not_34 (not_34_out, B);
  not not_35 (not_35_out, C);
  not not_36 (not_36_out, A);
  not not_37 (not_37_out, B);
  not not_38 (not_38_out, D);
  not not_39 (not_39_out, E);
  not not_40 (not_40_out, A);
  not not_41 (not_41_out, B);
  not not_42 (not_42_out, E);
  or or_1 (a_2, and_1_out, and_2_out);
  and and_3 (and_3_out, B, D);
  and and_4 (and_4_out, B, C);
  and and_5 (and_5_out, A, not_1_out);
  not not_43 (not_43_out, C);
  and and_6 (and_6_out, not_2_out, not_3_out);
  and and_7 (and_7_out, C, E);
  and and_8 (and_8_out, not_4_out, not_5_out);
  and and_9 (and_9_out, C, D);
  not not_44 (not_44_out, A);
  not not_45 (not_45_out, A);
  not not_46 (not_46_out, C);
  not not_47 (not_47_out, D);
  not not_48 (not_48_out, B);
  not not_49 (not_49_out, B);
  not not_50 (not_50_out, C);
  not not_51 (not_51_out, B);
  not not_52 (not_52_out, C);
  and and_10 (and_10_out, not_6_out, not_7_out);
  not not_53 (not_53_out, D);
  not not_54 (not_54_out, E);
  not not_55 (not_55_out, C);
  not not_56 (not_56_out, D);
  not not_57 (not_57_out, E);
  not not_58 (not_58_out, C);
  and and_11 (and_11_out, not_8_out, not_9_out);
  not not_59 (not_59_out, C);
  and and_12 (and_12_out, D, not_10_out);
  not not_60 (not_60_out, F);
  and and_13 (and_13_out, not_11_out, not_12_out);
  and and_14 (and_14_out, not_13_out, not_14_out);
  not not_61 (not_61_out, A);
  not not_62 (not_62_out, B);
  not not_63 (not_63_out, C);
  and and_15 (and_15_out, B, C);
  not not_64 (not_64_out, E);
  and and_16 (and_16_out, A, not_15_out);
  not not_65 (not_65_out, D);
  not not_66 (not_66_out, F);
  not not_67 (not_67_out, C);
  and and_17 (and_17_out, not_16_out, not_17_out);
  not not_68 (not_68_out, C);
  not not_69 (not_69_out, D);
  and and_18 (and_18_out, not_18_out, not_19_out);
  and and_19 (and_19_out, not_20_out, not_21_out);
  not not_70 (not_70_out, E);
  not not_71 (not_71_out, F);
  and and_20 (and_20_out, not_22_out, not_23_out);
  not not_72 (not_72_out, E);
  and and_21 (and_21_out, not_24_out, C);
  not not_73 (not_73_out, E);
  not not_74 (not_74_out, F);
  and and_22 (and_22_out, not_25_out, B);
  not not_75 (not_75_out, C);
  and and_23 (and_23_out, not_26_out, not_27_out);
  and and_24 (and_24_out, B, C);
  not not_76 (not_76_out, D);
  and and_25 (and_25_out, A, not_28_out);
  not not_77 (not_77_out, D);
  not not_78 (not_78_out, E);
  not not_79 (not_79_out, F);
  not not_80 (not_80_out, B);
  and and_26 (and_26_out, A, not_29_out);
  not not_81 (not_81_out, F);
  not not_82 (not_82_out, D);
  and and_27 (and_27_out, not_30_out, not_31_out);
  not not_83 (not_83_out, D);
  not not_84 (not_84_out, E);
  and and_28 (and_28_out, not_32_out, not_33_out);
  not not_85 (not_85_out, D);
  and and_29 (and_29_out, not_34_out, not_35_out);
  not not_86 (not_86_out, F);
  and and_30 (and_30_out, not_36_out, not_37_out);
  and and_31 (and_31_out, not_38_out, not_39_out);
  not not_87 (not_87_out, F);
  and and_32 (and_32_out, not_40_out, not_41_out);
  and and_33 (and_33_out, D, not_42_out);
  not not_88 (not_88_out, C);
  not not_89 (not_89_out, D);
  not not_90 (not_90_out, F);
  not not_91 (not_91_out, C);
  not not_92 (not_92_out, C);
  not not_93 (not_93_out, F);
  not not_94 (not_94_out, F);
  or or_2 (or_2_out, and_3_out, and_4_out);
  and and_34 (and_34_out, and_5_out, not_43_out);
  and and_35 (and_35_out, and_6_out, and_7_out);
  and and_36 (and_36_out, and_8_out, and_9_out);
  and and_37 (and_37_out, not_44_out, C);
  and and_38 (and_38_out, D, E);
  and and_39 (and_39_out, not_45_out, B);
  and and_40 (and_40_out, not_46_out, not_47_out);
  and and_41 (and_41_out, A, not_48_out);
  not not_95 (not_95_out, C);
  and and_42 (and_42_out, not_49_out, not_50_out);
  and and_43 (and_43_out, D, F);
  and and_44 (and_44_out, not_51_out, not_52_out);
  and and_45 (and_45_out, D, E);
  not not_96 (not_96_out, B);
  and and_46 (and_46_out, and_10_out, C);
  and and_47 (and_47_out, not_53_out, not_54_out);
  and and_48 (and_48_out, B, not_55_out);
  not not_97 (not_97_out, D);
  not not_98 (not_98_out, D);
  and and_49 (and_49_out, B, not_56_out);
  and and_50 (and_50_out, B, C);
  and and_51 (and_51_out, D, not_57_out);
  not not_99 (not_99_out, C);
  and and_52 (and_52_out, A, not_58_out);
  and and_53 (and_53_out, A, D);
  and and_54 (and_54_out, and_11_out, not_59_out);
  and and_55 (and_55_out, and_12_out, not_60_out);
  and and_56 (and_56_out, and_13_out, C);
  and and_57 (and_57_out, and_14_out, F);
  and and_58 (and_58_out, not_61_out, not_62_out);
  and and_59 (and_59_out, D, E);
  not not_100 (not_100_out, F);
  and and_60 (and_60_out, B, not_63_out);
  not not_101 (not_101_out, D);
  and and_61 (and_61_out, B, C);
  not not_102 (not_102_out, D);
  not not_103 (not_103_out, E);
  not not_104 (not_104_out, F);
  and and_62 (and_62_out, and_15_out, D);
  and and_63 (and_63_out, not_64_out, F);
  and and_64 (and_64_out, and_16_out, not_65_out);
  and and_65 (and_65_out, E, not_66_out);
  and and_66 (and_66_out, A, not_67_out);
  and and_67 (and_67_out, A, C);
  not not_105 (not_105_out, E);
  not not_106 (not_106_out, F);
  and and_68 (and_68_out, and_17_out, not_68_out);
  and and_69 (and_69_out, not_69_out, E);
  and and_70 (and_70_out, and_18_out, D);
  and and_71 (and_71_out, E, F);
  and and_72 (and_72_out, and_19_out, C);
  and and_73 (and_73_out, not_70_out, not_71_out);
  and and_74 (and_74_out, and_20_out, C);
  and and_75 (and_75_out, D, not_72_out);
  and and_76 (and_76_out, and_21_out, D);
  and and_77 (and_77_out, not_73_out, not_74_out);
  and and_78 (and_78_out, and_22_out, not_75_out);
  and and_79 (and_79_out, and_23_out, F);
  not not_107 (not_107_out, C);
  not not_108 (not_108_out, F);
  and and_80 (and_80_out, and_24_out, not_76_out);
  and and_81 (and_81_out, E, F);
  and and_82 (and_82_out, and_25_out, not_77_out);
  and and_83 (and_83_out, not_78_out, not_79_out);
  and and_84 (and_84_out, A, not_80_out);
  not not_109 (not_109_out, C);
  not not_110 (not_110_out, E);
  and and_85 (and_85_out, and_26_out, D);
  and and_86 (and_86_out, E, not_81_out);
  and and_87 (and_87_out, A, C);
  and and_88 (and_88_out, not_82_out, E);
  and and_89 (and_89_out, and_27_out, not_83_out);
  and and_90 (and_90_out, not_84_out, F);
  and and_91 (and_91_out, and_28_out, not_85_out);
  and and_92 (and_92_out, E, F);
  and and_93 (and_93_out, and_29_out, D);
  and and_94 (and_94_out, E, not_86_out);
  and and_95 (and_95_out, and_30_out, C);
  and and_96 (and_96_out, and_31_out, not_87_out);
  and and_97 (and_97_out, and_32_out, C);
  and and_98 (and_98_out, and_33_out, F);
  and and_99 (and_99_out, B, not_88_out);
  and and_100 (and_100_out, not_89_out, not_90_out);
  not not_111 (not_111_out, D);
  not not_112 (not_112_out, F);
  and and_101 (and_101_out, B, not_91_out);
  and and_102 (and_102_out, D, F);
  and and_103 (and_103_out, B, D);
  and and_104 (and_104_out, E, F);
  and and_105 (and_105_out, B, C);
  not not_113 (not_113_out, E);
  not not_114 (not_114_out, F);
  and and_106 (and_106_out, A, not_92_out);
  and and_107 (and_107_out, D, not_93_out);
  and and_108 (and_108_out, A, D);
  and and_109 (and_109_out, E, not_94_out);
  not not_115 (not_115_out, D);
  or or_3 (b_2, or_2_out, and_34_out);
  or or_4 (or_4_out, and_35_out, and_36_out);
  and and_110 (and_110_out, and_37_out, and_38_out);
  and and_111 (and_111_out, and_39_out, and_40_out);
  and and_112 (and_112_out, and_41_out, not_95_out);
  and and_113 (and_113_out, and_42_out, and_43_out);
  and and_114 (and_114_out, and_44_out, and_45_out);
  and and_115 (and_115_out, not_96_out, D);
  and and_116 (and_116_out, E, F);
  and and_117 (and_117_out, and_46_out, and_47_out);
  and and_118 (and_118_out, and_48_out, not_97_out);
  and and_119 (and_119_out, B, not_98_out);
  and and_120 (and_120_out, and_49_out, E);
  and and_121 (and_121_out, and_50_out, and_51_out);
  and and_122 (and_122_out, A, not_99_out);
  and and_123 (and_123_out, E, F);
  and and_124 (and_124_out, and_52_out, D);
  and and_125 (and_125_out, and_53_out, F);
  and and_126 (and_126_out, A, D);
  and and_127 (and_127_out, and_54_out, and_55_out);
  and and_128 (and_128_out, and_56_out, and_57_out);
  and and_129 (and_129_out, and_58_out, C);
  and and_130 (and_130_out, and_59_out, not_100_out);
  and and_131 (and_131_out, and_60_out, not_101_out);
  and and_132 (and_132_out, E, F);
  and and_133 (and_133_out, and_61_out, not_102_out);
  and and_134 (and_134_out, not_103_out, not_104_out);
  and and_135 (and_135_out, and_62_out, and_63_out);
  and and_136 (and_136_out, and_64_out, and_65_out);
  and and_137 (and_137_out, and_66_out, D);
  and and_138 (and_138_out, E, F);
  and and_139 (and_139_out, and_67_out, D);
  and and_140 (and_140_out, not_105_out, not_106_out);
  and and_141 (and_141_out, A, B);
  and and_142 (and_142_out, and_68_out, and_69_out);
  and and_143 (and_143_out, and_70_out, and_71_out);
  and and_144 (and_144_out, and_72_out, and_73_out);
  and and_145 (and_145_out, and_74_out, and_75_out);
  and and_146 (and_146_out, and_76_out, and_77_out);
  and and_147 (and_147_out, and_78_out, and_79_out);
  and and_148 (and_148_out, B, not_107_out);
  and and_149 (and_149_out, E, not_108_out);
  and and_150 (and_150_out, and_80_out, and_81_out);
  and and_151 (and_151_out, and_82_out, and_83_out);
  and and_152 (and_152_out, and_84_out, not_109_out);
  and and_153 (and_153_out, not_110_out, F);
  and and_154 (and_154_out, and_85_out, and_86_out);
  and and_155 (and_155_out, and_87_out, and_88_out);
  and and_156 (and_156_out, A, C);
  and and_157 (and_157_out, E, F);
  and and_158 (and_158_out, and_89_out, and_90_out);
  and and_159 (and_159_out, and_91_out, and_92_out);
  and and_160 (and_160_out, and_93_out, and_94_out);
  and and_161 (and_161_out, and_95_out, and_96_out);
  and and_162 (and_162_out, and_97_out, and_98_out);
  and and_163 (and_163_out, and_99_out, and_100_out);
  and and_164 (and_164_out, B, not_111_out);
  and and_165 (and_165_out, E, not_112_out);
  and and_166 (and_166_out, and_101_out, and_102_out);
  and and_167 (and_167_out, and_103_out, and_104_out);
  and and_168 (and_168_out, and_105_out, D);
  and and_169 (and_169_out, not_113_out, not_114_out);
  and and_170 (and_170_out, and_106_out, and_107_out);
  and and_171 (and_171_out, and_108_out, and_109_out);
  and and_172 (and_172_out, A, C);
  and and_173 (and_173_out, not_115_out, F);
  or or_5 (or_5_out, or_4_out, and_110_out);
  or or_6 (or_6_out, and_111_out, and_112_out);
  or or_7 (or_7_out, and_113_out, and_114_out);
  and and_174 (and_174_out, and_115_out, and_116_out);
  or or_8 (or_8_out, and_117_out, and_118_out);
  and and_175 (and_175_out, and_119_out, F);
  or or_9 (or_9_out, and_120_out, and_121_out);
  and and_176 (and_176_out, and_122_out, and_123_out);
  or or_10 (or_10_out, and_124_out, and_125_out);
  and and_177 (and_177_out, and_126_out, E);
  or or_11 (or_11_out, and_127_out, and_128_out);
  and and_178 (and_178_out, and_129_out, and_130_out);
  and and_179 (and_179_out, and_131_out, and_132_out);
  and and_180 (and_180_out, and_133_out, and_134_out);
  or or_12 (or_12_out, and_135_out, and_136_out);
  and and_181 (and_181_out, and_137_out, and_138_out);
  and and_182 (and_182_out, and_139_out, and_140_out);
  and and_183 (and_183_out, and_141_out, F);
  or or_13 (or_13_out, and_142_out, and_143_out);
  or or_14 (or_14_out, and_144_out, and_145_out);
  or or_15 (or_15_out, and_146_out, and_147_out);
  and and_184 (and_184_out, and_148_out, and_149_out);
  or or_16 (or_16_out, and_150_out, and_151_out);
  and and_185 (and_185_out, and_152_out, and_153_out);
  or or_17 (or_17_out, and_154_out, and_155_out);
  and and_186 (and_186_out, and_156_out, and_157_out);
  or or_18 (or_18_out, and_158_out, and_159_out);
  or or_19 (or_19_out, and_160_out, and_161_out);
  or or_20 (or_20_out, and_162_out, and_163_out);
  and and_187 (and_187_out, and_164_out, and_165_out);
  or or_21 (or_21_out, and_166_out, and_167_out);
  and and_188 (and_188_out, and_168_out, and_169_out);
  or or_22 (or_22_out, and_170_out, and_171_out);
  and and_189 (and_189_out, and_172_out, and_173_out);
  or or_23 (c_2, or_5_out, or_6_out);
  or or_24 (or_24_out, or_7_out, and_174_out);
  or or_25 (or_25_out, or_8_out, and_175_out);
  or or_26 (or_26_out, or_9_out, and_176_out);
  or or_27 (or_27_out, or_10_out, and_177_out);
  or or_28 (or_28_out, or_11_out, and_178_out);
  or or_29 (or_29_out, and_179_out, and_180_out);
  or or_30 (or_30_out, or_12_out, and_181_out);
  or or_31 (or_31_out, and_182_out, and_183_out);
  or or_32 (or_32_out, or_13_out, or_14_out);
  or or_33 (or_33_out, or_15_out, and_184_out);
  or or_34 (or_34_out, or_16_out, and_185_out);
  or or_35 (or_35_out, or_17_out, and_186_out);
  or or_36 (or_36_out, or_18_out, or_19_out);
  or or_37 (or_37_out, or_20_out, and_187_out);
  or or_38 (or_38_out, or_21_out, and_188_out);
  or or_39 (or_39_out, or_22_out, and_189_out);
  or or_40 (or_40_out, or_24_out, or_25_out);
  or or_41 (d_2, or_40_out, or_42_out);
  or or_42 (or_42_out, or_26_out, or_27_out);
  or or_43 (or_43_out, or_28_out, or_29_out);
  or or_44 (e_2, or_43_out, or_45_out);
  or or_45 (or_45_out, or_30_out, or_31_out);
  or or_46 (or_46_out, or_32_out, or_33_out);
  or or_47 (f_2, or_46_out, or_48_out);
  or or_48 (or_48_out, or_34_out, or_35_out);
  or or_49 (or_49_out, or_36_out, or_37_out);
  or or_50 (g_2, or_49_out, or_51_out);
  or or_51 (or_51_out, or_38_out, or_39_out);

  assign h = G;

  // Notes on the sheet:
  //   23CE004
endmodule

module _7Seg_0_to_99 (
  input  [6:0] in_1
);

  wire bcd_to_7seg_1_a_2, bcd_to_7seg_1_b_2, bcd_to_7seg_1_c_2, bcd_to_7seg_1_d_2, bcd_to_7seg_1_e,
       bcd_to_7seg_1_f, bcd_to_7seg_1_g, bcd_to_7seg_2_a_2, bcd_to_7seg_2_b_2, bcd_to_7seg_2_c_2,
       bcd_to_7seg_2_d_2, bcd_to_7seg_2_e, bcd_to_7seg_2_f, bcd_to_7seg_2_g, n7bit_to_bcd_1_a_2,
       n7bit_to_bcd_1_b_2, n7bit_to_bcd_1_c_2, n7bit_to_bcd_1_d_2, n7bit_to_bcd_1_e_2, n7bit_to_bcd_1_f_2,
       n7bit_to_bcd_1_g_2, n7bit_to_bcd_1_h;

  _7Bit_to_BCD u_7bit_to_bcd_1 (
    .A(in_1[6]), .B(in_1[5]), .C(in_1[4]), .D(in_1[3]), .E(in_1[2]), .F(in_1[1]), .G(in_1[0]),
    .a_2(n7bit_to_bcd_1_a_2), .b_2(n7bit_to_bcd_1_b_2), .c_2(n7bit_to_bcd_1_c_2), .d_2(n7bit_to_bcd_1_d_2),
    .e_2(n7bit_to_bcd_1_e_2), .f_2(n7bit_to_bcd_1_f_2), .g_2(n7bit_to_bcd_1_g_2), .h(n7bit_to_bcd_1_h));
  BCD_To_7Seg bcd_to_7seg_1 (
    .A(n7bit_to_bcd_1_a_2), .B(n7bit_to_bcd_1_b_2), .C(n7bit_to_bcd_1_c_2), .D(n7bit_to_bcd_1_d_2),
    .a_2(bcd_to_7seg_1_a_2), .b_2(bcd_to_7seg_1_b_2), .c_2(bcd_to_7seg_1_c_2), .d_2(bcd_to_7seg_1_d_2),
    .e(bcd_to_7seg_1_e), .f(bcd_to_7seg_1_f), .g(bcd_to_7seg_1_g));
  BCD_To_7Seg bcd_to_7seg_2 (
    .A(n7bit_to_bcd_1_e_2), .B(n7bit_to_bcd_1_f_2), .C(n7bit_to_bcd_1_g_2), .D(n7bit_to_bcd_1_h),
    .a_2(bcd_to_7seg_2_a_2), .b_2(bcd_to_7seg_2_b_2), .c_2(bcd_to_7seg_2_c_2), .d_2(bcd_to_7seg_2_d_2),
    .e(bcd_to_7seg_2_e), .f(bcd_to_7seg_2_f), .g(bcd_to_7seg_2_g));
  _7_Segment_Display u_7_segment_display_1 (
    .g(bcd_to_7seg_1_g), .f(bcd_to_7seg_1_f), .a(bcd_to_7seg_1_a_2), .b(bcd_to_7seg_1_b_2),
    .e(bcd_to_7seg_1_e), .d(bcd_to_7seg_1_d_2), .c(bcd_to_7seg_1_c_2));  // open: dp
  _7_Segment_Display u_7_segment_display_2 (
    .g(bcd_to_7seg_2_g), .f(bcd_to_7seg_2_f), .a(bcd_to_7seg_2_a_2), .b(bcd_to_7seg_2_b_2),
    .e(bcd_to_7seg_2_e), .d(bcd_to_7seg_2_d_2), .c(bcd_to_7seg_2_c_2));  // open: dp

  // Notes on the sheet:
  //   23CE004
endmodule
